// Logisim project ex-6.circ as structural Verilog: 1 circuit, main circuit main
module main (
  input  in_1
);

  wire and_1_out, clock_1_out, d_ff_1_q, d_ff_2_q, d_ff_3_q, d_ff_4_q, not_1_out, not_2_out;

  Clock clock_1 (.out(clock_1_out));
  D_Flip_Flop d_ff_1 (.clk(clock_1_out), .D(in_1), .Q(d_ff_1_q));  // open: Qn, preset, en, reset
  D_Flip_Flop d_ff_2 (.clk(clock_1_out), .Q(d_ff_2_q));  // open: D, Qn, preset, en, reset
  not not_1 (not_1_out, d_ff_1_q);
  D_Flip_Flop d_ff_3 (.clk(clock_1_out), .Q(d_ff_3_q));  // open: D, Qn, preset, en, reset
  not not_2 (not_2_out, d_ff_3_q);
  D_Flip_Flop d_ff_4 (.clk(clock_1_out), .D(d_ff_3_q), .Q(d_ff_4_q));  // open: Qn, preset, en, reset
  and and_1 (and_1_out, d_ff_4_q, not_2_out, d_ff_2_q, not_1_out);
  LED led_1 (.in(and_1_out));
endmodule
