// Logisim project exp-5.circ as structural Verilog: 1 circuit, main circuit main
module main (
  input  in_1,
  input  in_2,
  input  in_3,
  input  in_4
);

  wire clock_1_out, d_ff_2_q, d_ff_3_q, d_ff_4_q, undriven, undriven_2, undriven_3, undriven_4, undriven_5,
       xor_1_out;

  Clock clock_1 (.out(clock_1_out));
  LED led_1 ();  // open: in
  D_Flip_Flop d_ff_1 (.clk(clock_1_out), .D(d_ff_4_q), .en(undriven));  // open: Q, Qn, preset, reset
  LED led_2 (.in(d_ff_2_q));
  D_Flip_Flop d_ff_2 (.clk(clock_1_out), .D(xor_1_out), .Q(d_ff_2_q), .en(undriven_3));  // open: Qn, preset, reset
  xor xor_1 (xor_1_out, undriven_2, d_ff_4_q);
  LED led_3 (.in(d_ff_3_q));
  D_Flip_Flop d_ff_3 (.clk(clock_1_out), .D(d_ff_2_q), .Q(d_ff_3_q), .en(undriven_4));  // open: Qn, preset, reset
  D_Flip_Flop d_ff_4 (.clk(clock_1_out), .D(d_ff_3_q), .Q(d_ff_4_q), .en(undriven_5));  // open: Qn, preset, reset
  LED led_4 (.in(d_ff_4_q));
endmodule
